# Fritzing sketch RS (saved by Fritzing 0.9.2b)
circuit board: 15.0359cm x 10.1914cm
breadboards: 1

parts:
  S1 = Toggle Switch [package=THT]
  S2 = Toggle Switch [package=THT]
  R1 = Resistor [tolerance=±5% resistance=220 package=THT]
  LED1 = LED - 5mm [color="Red (633nm)" package="5 mm [THT]"]
  VCC1 = Battery
  M1 = DC Motor
  U1 = mystery part, 28 pins [chip_label=ＡＥ－ＡＴＭＥＧＡ３２８－ＭＩＮＩ]
  U2 = TA7291P [package=HSIP10-P-2.54(THT)]
  U3 = TA7291P [package=HSIP10-P-2.54(THT)]
  U4 = TA7291P [package=HSIP10-P-2.54(THT)]
  M2 = DC Motor
  M3 = DC Motor
  VCC2 = Battery
  LED2 = LED - 5mm [color="Red (633nm)" package="5 mm [THT]"]
  R2 = Resistor [tolerance=±5% resistance=220 package=THT]
  U6 = mystery part, 20 pins [chip_label=?]  # not connected
  U5 = mystery part, 20 pins [chip_label=?]

nets:
  N1: S1.L1, R1.Pin_1, U1.pin13
  N2: S1.L2, VCC1.+, VCC2.-, LED2.anode, U5.pin20
  N3: S2.COM, VCC2.+
  N4: S2.L2, U2.Vs, U4.Vs, R2.Pin_0
  N5: R1.Pin_0, LED1.cathode
  N6: LED1.anode, VCC1.-, U1.pin11
  N7: M1.pin_1, U2.OUT1
  N8: M1.pin_2, U2.OUT2
  N9: U1.pin17, U4.IN2
  N10: U1.pin18, U4.IN1
  N11: U1.pin21, U4.Vref
  N12: U1.pin22, U3.IN2
  N13: U1.pin23, U3.IN1
  N14: U1.pin24, U3.Vref
  N15: U1.pin26, U2.Vref, U2.IN2
  N16: U1.pin27, U2.IN1
  GND: U2.GND, U4.GND, U5.pin11
  VCC: U2.Vcc, U4.Vcc
  N17: U3.OUT1, M2.pin_1
  N18: U3.OUT2, M2.pin_2
  N19: U4.OUT1, M3.pin_1
  N20: U4.OUT2, M3.pin_2
  N21: LED2.cathode, R2.Pin_1

custom parts:
  TA7291P: The IC are Full-Bridge Driver. 4 modes available (CW / CCW / STOP / BRAKE) and PWM control. Output current:1.0 A (AVE.) 2.0 A (PEAK)
